# Fritzing sketch bme280 (saved by Fritzing 0.9.3b)
breadboards: 1

parts:
  NodeMCU3 = NodeMCU V3.0
  BME-280 = Adafruit BME280

nets:
  3V3: NodeMCU3.3V3, BME-280.VIN
  N1: NodeMCU3.GND#6, NodeMCU3.GND#13, NodeMCU3.GND#16, NodeMCU3.GND#33, BME-280.GND
  N2: NodeMCU3.D5, BME-280.SCK/SCL
  N3: NodeMCU3.D6, BME-280.SDI/SDA
  N4: NodeMCU3.D7, BME-280.CS
  N5: NodeMCU3.D8, BME-280.SDO/ADR

custom parts:
  NodeMCU V3.0: ESP8266 based NodeMCU
  Adafruit BME280: Bosch has stepped up their game with their new BME280 sensor, an environmental sensor with temperature, barometric pressure and humidity! This sensor is great for all sorts of weather/environmental sensing and can even be used in both I2C and SPI! This precision sensor from Bosch is the best low-cost sensing solution for measuring humidity with ±3% accuracy, barometric pressure with ±1 hPa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
