# Fritzing sketch ccs811 (saved by Fritzing 0.9.3b)
breadboards: 1

parts:
  NodeMCU1 = NodeMCU V3.0
  Part1 = Adafruit CCS811

nets:
  N1: NodeMCU1.D1, Part1.SCL
  N2: NodeMCU1.D2, Part1.SDA
  3V3: NodeMCU1.3V3, Part1.VIN
  N3: NodeMCU1.GND#6, NodeMCU1.GND#13, NodeMCU1.GND#16, NodeMCU1.GND#33, Part1.GND, Part1.!WAKE

custom parts:
  NodeMCU V3.0: ESP8266 based NodeMCU
