# Fritzing sketch dfplayer (saved by Fritzing 0.9.3b)
breadboards: 1

parts:
  Part1 = Arduino Nano (Rev3.0)
  DFRobot_DFPlayer_Mini1 = DFRobot DFPlayer Mini [part_number=DFR0299]
  J1 = Piezo Speaker

nets:
  N1: Part1.GND, DFRobot_DFPlayer_Mini1.GND-1, DFRobot_DFPlayer_Mini1.GND-2
  N2: Part1.D9, DFRobot_DFPlayer_Mini1.BUSY
  N3: Part1.D10, DFRobot_DFPlayer_Mini1.TX
  N4: Part1.D11/MOSI, DFRobot_DFPlayer_Mini1.RX
  5V: Part1.5V, DFRobot_DFPlayer_Mini1.VCC
  N5: DFRobot_DFPlayer_Mini1.SPK_1, J1.pin2
  N6: DFRobot_DFPlayer_Mini1.SPK_2, J1.pin1
