# Fritzing sketch ds18b20 (saved by Fritzing 0.9.4)
circuit board: 3.98663cm x 3.47791cm
breadboards: 1

parts:
  NodeMCU = ESP8266 NodeMCU LoLin module
  Pull_Up = Resistor [tolerance=±5% resistance=4.7k package=THT]
  DS18B20_1 = DS18B20 1-Wire Temperature Sensor [part_number=DS18B20]

nets:
  N1: NodeMCU.D0, Pull_Up.Pin_0, DS18B20_1.DQ
  GND: NodeMCU.GND, DS18B20_1.GND
  VIN: NodeMCU.Vin, Pull_Up.Pin_1, DS18B20_1.VDD

custom parts:
  ESP8266 NodeMCU LoLin module: ESP8266 based NodeMCU
