# Fritzing sketch dust_sensor (saved by Fritzing 0.9.3b)

parts:
  NodeMCU = NodeMCU V3.0
  OLED_Display_SSD1306 = OLED Monochrome 128x64 0.96 inch [part_number=326]
  SDS011 = mystery part, 7 pins [chip_label=SDS011]

nets:
  N1: NodeMCU.D1, SDS011.pin1
  N2: NodeMCU.D2, SDS011.pin2
  N3: NodeMCU.D3, OLED_Display_SSD1306.RESET
  N4: NodeMCU.D4, OLED_Display_SSD1306.DC_SA0
  3V3: NodeMCU.3V3, OLED_Display_SSD1306.3.3V
  N5: NodeMCU.GND#6, NodeMCU.GND#13, NodeMCU.GND#33, OLED_Display_SSD1306.GND
  N6: NodeMCU.D5, OLED_Display_SSD1306.MOSI_SDA
  N7: NodeMCU.D7, OLED_Display_SSD1306.SCLK_SCK
  N8: NodeMCU.D8, OLED_Display_SSD1306.CS
  N9: NodeMCU.VU, SDS011.pin5
  N10: NodeMCU.GND#41, SDS011.pin3

custom parts:
  NodeMCU V3.0: ESP8266 based NodeMCU
  OLED Monochrome 128x64 0.96 inch: These displays are small, only about 1" diameter, but very readable due to the high contrast of an OLED display. This display is made of 128x64 individual white OLED pixels, each one is turned on or off by the controller chip. Because the display makes its own light, no backlight is required. This reduces the power required to run the OLED and is why the display has such high contrast; we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
