# Fritzing sketch flowsensor (saved by Fritzing 0.9.3b)

parts:
  NodeMCU1 = NodeMCU V3.0
  OLED_Display_SSD1307 = OLED Monochrome 128x64 0.96 inch [part_number=326]
  FS300A_Flow_Meter = YF-S201 Water Flow Meter

nets:
  N1: NodeMCU1.D2, FS300A_Flow_Meter.SIG
  N2: NodeMCU1.D3, OLED_Display_SSD1307.RESET
  N3: NodeMCU1.D4, OLED_Display_SSD1307.DC_SA0
  3V3: NodeMCU1.3V3, OLED_Display_SSD1307.3.3V
  N4: NodeMCU1.GND#6, NodeMCU1.GND#13, NodeMCU1.GND#33, OLED_Display_SSD1307.GND
  N5: NodeMCU1.D5, OLED_Display_SSD1307.MOSI_SDA
  N6: NodeMCU1.D7, OLED_Display_SSD1307.SCLK_SCK
  N7: NodeMCU1.D8, OLED_Display_SSD1307.CS
  N8: NodeMCU1.VU, FS300A_Flow_Meter.VCC
  N9: NodeMCU1.GND#41, FS300A_Flow_Meter.GND

custom parts:
  NodeMCU V3.0: ESP8266 based NodeMCU
  OLED Monochrome 128x64 0.96 inch: These displays are small, only about 1" diameter, but very readable due to the high contrast of an OLED display. This display is made of 128x64 individual white OLED pixels, each one is turned on or off by the controller chip. Because the display makes its own light, no backlight is required. This reduces the power required to run the OLED and is why the display has such high contrast; we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
  YF-S201 Water Flow Meter: The YF-S201 Flow Meter. The input voltage is 5V to 24V (DC).
