# Fritzing sketch relay (saved by Fritzing 0.9.3b)

parts:
  NodeMCU = NodeMCU V3.0
  OLED_Display_SSD1308 = OLED Monochrome 128x64 0.96 inch [part_number=326]
  4_Channel_Relay = 4 Channel Power Relay

nets:
  N1: NodeMCU.D0, 4_Channel_Relay.IN1
  N2: NodeMCU.D1, 4_Channel_Relay.IN2
  N3: NodeMCU.D2, 4_Channel_Relay.IN3
  N4: NodeMCU.D3, OLED_Display_SSD1308.RESET
  N5: NodeMCU.D4, OLED_Display_SSD1308.DC_SA0
  3V3: NodeMCU.3V3, OLED_Display_SSD1308.3.3V
  N6: NodeMCU.GND#6, NodeMCU.GND#13, NodeMCU.GND#33, OLED_Display_SSD1308.GND
  N7: NodeMCU.D5, OLED_Display_SSD1308.MOSI_SDA
  N8: NodeMCU.D6, 4_Channel_Relay.IN4
  N9: NodeMCU.D7, OLED_Display_SSD1308.SCLK_SCK
  N10: NodeMCU.D8, OLED_Display_SSD1308.CS
  N11: NodeMCU.VU, 4_Channel_Relay.VCC#13
  N12: NodeMCU.GND#41, 4_Channel_Relay.GND
  N13: 4_Channel_Relay.VCC#14, 4_Channel_Relay.JD-VCC

custom parts:
  NodeMCU V3.0: ESP8266 based NodeMCU
  OLED Monochrome 128x64 0.96 inch: These displays are small, only about 1" diameter, but very readable due to the high contrast of an OLED display. This display is made of 128x64 individual white OLED pixels, each one is turned on or off by the controller chip. Because the display makes its own light, no backlight is required. This reduces the power required to run the OLED and is why the display has such high contrast; we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
  4 Channel Power Relay: A 4 channel power relay. The module operates at 5V.
