# Fritzing sketch tsl2561 (saved by Fritzing 0.9.3b)
breadboards: 1

parts:
  NodeMCU2 = NodeMCU V3.0
  TSL2561 = Adafruit TSL2561 [part_number="Adafruit #439"]

nets:
  N1: NodeMCU2.D1, TSL2561.SCL
  N2: NodeMCU2.D2, TSL2561.SDA
  3V3: NodeMCU2.3V3, TSL2561.VIN
  N3: NodeMCU2.GND#6, NodeMCU2.GND#13, NodeMCU2.GND#16, NodeMCU2.GND#33, TSL2561.GND

custom parts:
  NodeMCU V3.0: ESP8266 based NodeMCU
  Adafruit TSL2561: The TSL2561 luminosity sensor is an advanced digital light sensor, ideal for use in a wide range of light situations. Compared to low cost CdS cells, this sensor is more precise, allowing for exact lux calculations and can be configured for different gain/timing ranges to detect light ranges from up to 0.1 - 40,000+ Lux on the fly. The best part of this sensor is that it contains both infrared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
