# Fritzing sketch garden (saved by Fritzing 0.9.10b)
breadboards: 1

parts:
  NodeMCU_Lolin = ESP8266 NodeMCU LoLin module
  Flow_PullUp = Resistor [tolerance=±5% resistance=10k power=0.25 package=THT]
  Flow = male pin header, 3 pins [form="♂ (male)"]
  Relay = male pin header, 6 pins [form="♂ (male)"]
  DS18B20 = DS18B20 1-Wire Temperature Sensor [part_number=DS18B20]
  DS18B20_2 = male pin header, 3 pins [form="♂ (male)"]
  4_Channel_Relay_Card = 4 Channel Power Relay
  YF-S201_Flow_Meter1 = YF-S201 Water Flow Meter
  BME-280 = male pin header, 6 pins [form="♂ (male)"]
  BME-280_2 = GY-BMEP280 Barometric Pressure Sensor - Breakout
  OLED1 = OLED 128x64 I2C Monochrome Display
  Display = male pin header, 4 pins [form="♂ (male)"]
  Temp_PullUp = Resistor [tolerance=±5% resistance=4.7k power=0.25 package=THT]

nets:
  N1: NodeMCU_Lolin.D0, NodeMCU_Lolin.RST
  N2: NodeMCU_Lolin.D1, Flow_PullUp.Pin_1, Flow.pin1, YF-S201_Flow_Meter1.SIG
  N3: NodeMCU_Lolin.D2, DS18B20.DQ, DS18B20_2.pin2, Temp_PullUp.Pin_1
  N4: NodeMCU_Lolin.D3, BME-280.pin3, BME-280_2.SCL
  N5: NodeMCU_Lolin.D4, BME-280.pin4, BME-280_2.SDA
  VCC: NodeMCU_Lolin.3V3, Flow_PullUp.Pin_0, Flow.pin2, Relay.pin1, DS18B20.VDD, DS18B20_2.pin3, 4_Channel_Relay_Card.VCC, YF-S201_Flow_Meter1.VCC, BME-280.pin1, BME-280_2.VCC, OLED1.VDD, Display.pin3, Temp_PullUp.Pin_0
  GND: NodeMCU_Lolin.GND, Flow.pin3, Relay.pin6, DS18B20.GND, DS18B20_2.pin1, 4_Channel_Relay_Card.GND, YF-S201_Flow_Meter1.GND, BME-280.pin2, BME-280_2.GND, OLED1.GND, Display.pin4
  N6: NodeMCU_Lolin.D5, Relay.pin5, 4_Channel_Relay_Card.IN1
  N7: NodeMCU_Lolin.D6, Relay.pin4, 4_Channel_Relay_Card.IN2
  N8: NodeMCU_Lolin.D7, Relay.pin3, 4_Channel_Relay_Card.IN3
  N9: NodeMCU_Lolin.D8, Relay.pin2, 4_Channel_Relay_Card.IN4
  N10: OLED1.SCK, Display.pin2
  N11: OLED1.SDA, Display.pin1

notes:
  v1.0
  garden

custom parts:
  ESP8266 NodeMCU LoLin module: ESP8266 based NodeMCU
  4 Channel Power Relay: A 4 channel power relay. The module operates at 5V.
  YF-S201 Water Flow Meter: The YF-S201 Flow Meter. The input voltage is 5V to 24V (DC).
  GY-BMEP280 Barometric Pressure Sensor - Breakout: The BME280 is a chip which was originally designed for the next generation of smartphones. It is made up of a very accurate pressure sensor and an associated temperature sensor which helps calibrate the pressure readings. And just for fun they threw in a pretty solid humidity sensor in there as well! So with an I2C connection you have access to enough weather data to make some pretty good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
