# Fritzing sketch sortinghat (saved by Fritzing 0.9.3b)
breadboards: 1

parts:
  Part1 = Arduino Nano (Rev3.0) (ICSP)
  DFRobot_DFPlayer_Mini1 = DFRobot DFPlayer Mini [part_number=DFR0299]
  Part2 = 12 NeoPixel Ring [part_number=1643]
  Part3 = 12 NeoPixel Ring [part_number=1643]
  J1 = Piezo Speaker
  R2 = Resistor [tolerance=±5% resistance=1M package="0603 [SMD]"]
  R1 = Resistor [tolerance=±5% resistance=10k package=THT]

nets:
  GND: Part1.GND, DFRobot_DFPlayer_Mini1.GND-1, DFRobot_DFPlayer_Mini1.GND-2, Part2.GND, Part3.GND
  N1: Part1.D2, Part2.IN, Part3.IN
  N2: Part1.D5, R2.Pin_0
  N3: Part1.D6, R2.Pin_1
  N4: Part1.D10, DFRobot_DFPlayer_Mini1.RX, R1.Pin_0, R1.Pin_1
  N5: Part1.D11/MOSI, DFRobot_DFPlayer_Mini1.TX
  5V: Part1.5V, DFRobot_DFPlayer_Mini1.VCC
  VDD: Part1.3V3, Part2.VDD, Part3.VDD
  N6: DFRobot_DFPlayer_Mini1.SPK_1, J1.pin2
  N7: DFRobot_DFPlayer_Mini1.SPK_2, J1.pin1

notes:
  Open end as button

custom parts:
  12 NeoPixel Ring: 12 ultra bright smart LED NeoPixels are arranged in a circle with 1.5" (37mm) outer diameter. The rings are 'chainable' - connect the output pin of one to the input pin of another. Use only one microcontroller pin to control as many as you can chain together! Each LED is addressable as the driver chip is inside the LED. Each one has ~18mA constant current drive so the color will be very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
